# Fritzing sketch arduinoSchem (saved by Fritzing 0.9.3b)
circuit board: 8.46667cm x 5.64444cm
breadboards: 2

parts:
  Composant1 = Arduino Mega 2560 (Rev3)
  B3 = Pushbutton [package="[THT]"]
  B1 = Pushbutton [package="[THT]"]
  B2 = Pushbutton [package="[THT]"]
  SS2 = 7-SEGMENT-4DIGIT-YOUNGSUN [package=7-segment-4digit-youngsun]
  B4 = Pushbutton [package="[THT]"]
  L6 = LED - 5mm [color="Red (633nm)" package="5 mm [THT]"]
  L7 = LED - 5mm [color="Red (633nm)" package="5 mm [THT]"]
  L5 = LED - 5mm [color="Red (633nm)" package="5 mm [THT]"]
  L1 = LED - 5mm [color="Red (633nm)" package="5 mm [THT]"]
  L2 = LED - 5mm [color="Red (633nm)" package="5 mm [THT]"]
  L3 = LED - 5mm [color="Red (633nm)" package="5 mm [THT]"]
  L4 = LED - 5mm [color="Red (633nm)" package="5 mm [THT]"]
  R1 = Resistor [tolerance=±5% resistance=220 package=THT]
  R2 = Resistor [tolerance=±5% resistance=220 package=THT]  # not connected
  R3 = Resistor [tolerance=±5% resistance=220 package=THT]
  R5 = Resistor [tolerance=±5% resistance=220 package=THT]
  R6 = Resistor [tolerance=±5% resistance=220 package=THT]
  R7 = Resistor [tolerance=±5% resistance=220 package=THT]
  R8 = Resistor [tolerance=±5% resistance=220 package=THT]
  R9 = Resistor [tolerance=±5% resistance=220 package=THT]
  R12 = Resistor [tolerance=±5% resistance=10k package=THT]
  R13 = Resistor [tolerance=±5% resistance=10k package=THT]
  R14 = Resistor [tolerance=±5% resistance=10k package=THT]
  Composant3 = NRF24L01
  C1 = Ceramic Capacitor [capacitance=100nF package="100 mil [THT, multilayer]"]
  SS1 = 7-SEGMENT-4DIGIT-YOUNGSUN [package=7-segment-4digit-youngsun-longpads]  # not connected

nets:
  N1: Composant1.D19/RX1, Composant3.CE
  N2: Composant1.D14/TX3, Composant1.5V, Composant1.D0_RX0, Composant1.D1_TX0, Composant1.D2_PWM, B3.Pin_3, B3.Pin_4, B1.Pin_3, B1.Pin_4, B2.Pin_3, B2.Pin_4, B4.Pin_3, B4.Pin_4
  GND: Composant1.GND, L6.cathode, L7.cathode, L5.cathode, L1.cathode, L2.cathode, L3.cathode, L4.cathode, R9.Pin_1, R12.Pin_0, R13.Pin_0, R14.Pin_0, Composant3.GND, C1.0
  N3: Composant1.D9_PWM, SS2.DIG4
  N4: Composant1.D8_PWM, SS2.DIG3
  3V3: Composant1.3V3, Composant3.VCC, C1.1
  N5: Composant1.D6_PWM, SS2.DIG1
  N6: Composant1.D7_PWM, SS2.DIG2
  N7: Composant1.D23, SS2.B
  N8: Composant1.D25, SS2.D
  N9: Composant1.D27, SS2.G
  N10: Composant1.D29, SS2.A
  N11: Composant1.D31, SS2.C
  N12: Composant1.D33, SS2.F
  N13: Composant1.D35, SS2.E
  N14: Composant1.D37, SS2.DP
  N15: Composant1.D42, R5.Pin_1
  N16: Composant1.D43, R6.Pin_1
  N17: Composant1.D44, R1.Pin_1
  N18: Composant1.D45, R3.Pin_1
  N19: Composant1.D47, R7.Pin_1
  N20: Composant1.D48, R8.Pin_1
  N21: Composant1.D50, Composant3.MISO
  N22: Composant1.D51, Composant3.MOSI
  N23: Composant1.D52, Composant3.SCK
  N24: Composant1.D53, Composant3.CSN
  N25: B3.Pin_1, B3.Pin_2, R12.Pin_1
  N26: B1.Pin_1, B1.Pin_2, R14.Pin_1
  N27: B2.Pin_1, B2.Pin_2, R13.Pin_1
  N28: B4.Pin_1, B4.Pin_2, R9.Pin_0
  N29: L6.anode, R5.Pin_0
  N30: L7.anode, R6.Pin_0
  N31: L5.anode, R7.Pin_0
  N32: L1.anode, R1.Pin_0
  N33: L3.anode, R3.Pin_0
  N34: L4.anode, R8.Pin_0
